// Logisim project hw2.circ as structural Verilog: 1 circuit, main circuit main
module main (
  input  A1,
  input  A0,
  input  B1,
  input  B0,
  input  S1,
  input  S0
);

  wire n3_to_8_decoder_74138_1_p7, n3_to_8_decoder_74138_1_p8, n3_to_8_decoder_74138_1_p9,
       n3_to_8_decoder_74138_1_p10, not_1_out, not_2_out, not_3_out, not_4_out;

  not not_1 (not_1_out, A1);
  not not_2 (not_2_out, B1);
  not not_3 (not_3_out, A0);
  not not_4 (not_4_out, B0);
  // _3_to_8_decoder__74138 #(.Facing("east")) 3_to_8_decoder_74138_1: pin names not known; wires that end beside it: S0, S1, 1'b1, 1'b1, 1'b0, 1'b0, n3_to_8_decoder_74138_1_p7, n3_to_8_decoder_74138_1_p8, n3_to_8_decoder_74138_1_p9, n3_to_8_decoder_74138_1_p10
  // NOT_Gate not_5 has open pins: in=n3_to_8_decoder_74138_1_p7, out=open
  // NOT_Gate not_6 has open pins: in=n3_to_8_decoder_74138_1_p8, out=open
  // NOT_Gate not_7 has open pins: in=n3_to_8_decoder_74138_1_p9, out=open
  // NOT_Gate not_8 has open pins: in=n3_to_8_decoder_74138_1_p10, out=open
endmodule
